# Fritzing sketch wiring (saved by Fritzing 0.9.4)
breadboards: 1

parts:
  J2 = female pin header, 15 pins [form="♀ (female)"]  # not connected
  J3 = female pin header, 15 pins [form="♀ (female)"]
  J4 = female pin header, 17 pins [form="♀ (female)"]  # not connected
  J5 = female pin header, 17 pins [form="♀ (female)"]
  J6 = female pin header, 10 pins [form="♀ (female)"]  # not connected
  J7 = female pin header, 10 pins [form="♀ (female)"]
  J8 = female pin header, 8 pins [form="♀ (female)"]
  J9 = female pin header, 8 pins [form="♀ (female)"]  # not connected
  J10 = female pin header, 6 pins [form="♀ (female)"]
  J11 = female pin header, 4 pins [form="♀ (female)"]
  J12 = female pin header, 3 pins [form="♀ (female)"]
  J13 = female pin header, 1 pin [form="♀ (female)"]
  J15 = female pin header, 3 pins [form="♀ (female)"]
  J14 = female pin header, 3 pins [form="♀ (female)"]
  J16 = female pin header, 2 pins [form="♀ (female)"]

nets:
  N1: J3.pin2, J14.pin3
  N2: J5.pin14, J10.pin3, J11.pin2
  N3: J5.pin15, J10.pin1, J11.pin4
  N4: J7.pin10, J13.pin1
  N5: J8.pin5, J14.pin2
  N6: J8.pin6, J14.pin1
  N7: J10.pin2, J11.pin3
  N8: J10.pin4, J11.pin1, J12.pin3, J15.pin1
  N9: J10.pin5, J12.pin1, J15.pin2, J16.pin2
  N10: J10.pin6, J12.pin2, J15.pin3, J16.pin1

notes:
  12V
